// Logisim project Banco de Registradores.circ as structural Verilog: 7 circuits, main circuit registrador
module bando_registrador_8bits (
  input  [3:0] RX_select,
  input  LEITURA,
  input  [7:0] Entrada,
  input  [3:0] Ry_select,
  input  Escrever,
  input  [3:0] select,
  output [7:0] Rx,
  output [7:0] Ry
);

  wire demult_1x16_1_bit_1__0, demult_1x16_1_bit_1__1, demult_1x16_1_bit_1__2, demult_1x16_1_bit_1__3,
       demult_1x16_1_bit_1__4, demult_1x16_1_bit_1__5, demult_1x16_1_bit_1__6, demult_1x16_1_bit_1__7,
       demult_1x16_1_bit_1__8, demult_1x16_1_bit_1__9, demult_1x16_1_bit_1__10, demult_1x16_1_bit_1__11,
       demult_1x16_1_bit_1__12, demult_1x16_1_bit_1__13, demult_1x16_1_bit_1__14, demult_1x16_1_bit_1__15;
  wire [7:0] \registrador_1_saída , \registrador_2_saída , \registrador_3_saída , \registrador_4_saída ,
       \registrador_5_saída , \registrador_6_saída , \registrador_7_saída , \registrador_8_saída ,
       \registrador_9_saída , \registrador_10_saída , \registrador_11_saída , \registrador_12_saída ,
       \registrador_13_saída , \registrador_14_saída , \registrador_15_saída , \registrador_16_saída ;

  DEMULT_1x16_1_bit demult_1x16_1_bit_1 (
    .KEY(select), .l(Escrever), ._0(demult_1x16_1_bit_1__0), ._1(demult_1x16_1_bit_1__1),
    ._2(demult_1x16_1_bit_1__2), ._3(demult_1x16_1_bit_1__3), ._4(demult_1x16_1_bit_1__4),
    ._5(demult_1x16_1_bit_1__5), ._6(demult_1x16_1_bit_1__6), ._7(demult_1x16_1_bit_1__7),
    ._8(demult_1x16_1_bit_1__8), ._9(demult_1x16_1_bit_1__9), ._10(demult_1x16_1_bit_1__10),
    ._11(demult_1x16_1_bit_1__11), ._12(demult_1x16_1_bit_1__12), ._13(demult_1x16_1_bit_1__13),
    ._14(demult_1x16_1_bit_1__14), ._15(demult_1x16_1_bit_1__15));
  registrador registrador_1 (.entrada(Entrada), .CLOCK(demult_1x16_1_bit_1__0), .\saída (\registrador_1_saída ));
  registrador registrador_2 (.entrada(Entrada), .CLOCK(demult_1x16_1_bit_1__1), .\saída (\registrador_2_saída ));
  registrador registrador_3 (.entrada(Entrada), .CLOCK(demult_1x16_1_bit_1__2), .\saída (\registrador_3_saída ));
  registrador registrador_4 (.entrada(Entrada), .CLOCK(demult_1x16_1_bit_1__3), .\saída (\registrador_4_saída ));
  registrador registrador_5 (.entrada(Entrada), .CLOCK(demult_1x16_1_bit_1__4), .\saída (\registrador_5_saída ));
  registrador registrador_6 (.entrada(Entrada), .CLOCK(demult_1x16_1_bit_1__5), .\saída (\registrador_6_saída ));
  registrador registrador_7 (.entrada(Entrada), .CLOCK(demult_1x16_1_bit_1__6), .\saída (\registrador_7_saída ));
  registrador registrador_8 (.entrada(Entrada), .CLOCK(demult_1x16_1_bit_1__7), .\saída (\registrador_8_saída ));
  registrador registrador_9 (.entrada(Entrada), .CLOCK(demult_1x16_1_bit_1__8), .\saída (\registrador_9_saída ));
  registrador registrador_10 (.entrada(Entrada), .CLOCK(demult_1x16_1_bit_1__9), .\saída (\registrador_10_saída ));
  registrador registrador_11 (.entrada(Entrada), .CLOCK(demult_1x16_1_bit_1__10), .\saída (\registrador_11_saída ));
  registrador registrador_12 (.entrada(Entrada), .CLOCK(demult_1x16_1_bit_1__11), .\saída (\registrador_12_saída ));
  registrador registrador_13 (.entrada(Entrada), .CLOCK(demult_1x16_1_bit_1__12), .\saída (\registrador_13_saída ));
  registrador registrador_14 (.entrada(Entrada), .CLOCK(demult_1x16_1_bit_1__13), .\saída (\registrador_14_saída ));
  registrador registrador_15 (.entrada(Entrada), .CLOCK(demult_1x16_1_bit_1__14), .\saída (\registrador_15_saída ));
  registrador registrador_16 (.entrada(Entrada), .CLOCK(demult_1x16_1_bit_1__15), .\saída (\registrador_16_saída ));
  MULT_16X1 mult_16x1_1 (
    ._0(\registrador_1_saída ), ._1(\registrador_2_saída ), ._2(\registrador_3_saída ),
    ._3(\registrador_4_saída ), ._4(\registrador_5_saída ), ._5(\registrador_6_saída ),
    ._6(\registrador_7_saída ), ._7(\registrador_8_saída ), ._8(\registrador_9_saída ),
    ._9(\registrador_10_saída ), ._10(\registrador_11_saída ), ._11(\registrador_12_saída ),
    ._12(\registrador_13_saída ), ._13(\registrador_14_saída ), ._14(\registrador_15_saída ),
    ._15(\registrador_16_saída ), .CHAVE(RX_select), .\SAÍDA (Rx), .S(LEITURA));
  MULT_16X1 mult_16x1_2 (
    ._0(\registrador_1_saída ), ._1(\registrador_2_saída ), ._2(\registrador_3_saída ),
    ._3(\registrador_4_saída ), ._4(\registrador_5_saída ), ._5(\registrador_6_saída ),
    ._6(\registrador_7_saída ), ._7(\registrador_8_saída ), ._8(\registrador_9_saída ),
    ._9(\registrador_10_saída ), ._10(\registrador_11_saída ), ._11(\registrador_12_saída ),
    ._12(\registrador_13_saída ), ._13(\registrador_14_saída ), ._14(\registrador_15_saída ),
    ._15(\registrador_16_saída ), .CHAVE(Ry_select), .\SAÍDA (Ry), .S(LEITURA));
endmodule

module registrador (
  input  [7:0] entrada,
  input  CLOCK,
  output [7:0] \saída 
);

  flipflop_D flipflop_d_1 (.D(entrada[0]), .CLK(CLOCK), .out_3(\saída [0]));  // open: out_4
  flipflop_D flipflop_d_2 (.D(entrada[1]), .CLK(CLOCK), .out_3(\saída [1]));  // open: out_4
  flipflop_D flipflop_d_3 (.D(entrada[2]), .CLK(CLOCK), .out_3(\saída [2]));  // open: out_4
  flipflop_D flipflop_d_4 (.D(entrada[3]), .CLK(CLOCK), .out_3(\saída [3]));  // open: out_4
  flipflop_D flipflop_d_5 (.D(entrada[4]), .CLK(CLOCK), .out_3(\saída [4]));  // open: out_4
  flipflop_D flipflop_d_6 (.D(entrada[5]), .CLK(CLOCK), .out_3(\saída [5]));  // open: out_4
  flipflop_D flipflop_d_7 (.D(entrada[6]), .CLK(CLOCK), .out_3(\saída [6]));  // open: out_4
  flipflop_D flipflop_d_8 (.D(entrada[7]), .CLK(CLOCK), .out_3(\saída [7]));  // open: out_4
endmodule

module flipflop_D (
  input  D,
  input  CLK,
  output out_3,
  output out_4
);

  wire nand_1_out, nand_2_out, not_1_out;

  not not_1 (not_1_out, D);
  nand nand_1 (nand_1_out, D, CLK);
  nand nand_2 (nand_2_out, not_1_out, CLK);
  nand nand_3 (out_3, nand_1_out, out_4);
  nand nand_4 (out_4, out_3, nand_2_out);
endmodule

module DEMULT_1x16_1_bit (
  input  [3:0] KEY,
  input  l,
  output _0,
  output _1,
  output _2,
  output _3,
  output _4,
  output _5,
  output _6,
  output _7,
  output _8,
  output _9,
  output _10,
  output _11,
  output _12,
  output _13,
  output _14,
  output _15
);

  wire not_1_out, not_2_out, not_3_out, not_4_out;

  not not_1 (not_1_out, KEY[0]);
  not not_2 (not_2_out, KEY[1]);
  not not_3 (not_3_out, KEY[2]);
  not not_4 (not_4_out, KEY[3]);
  and and_1 (_0, l, not_1_out, not_2_out, not_3_out, not_4_out);
  and and_2 (_1, l, KEY[0], not_2_out, not_3_out, not_4_out);
  and and_3 (_2, l, not_1_out, KEY[1], not_3_out, not_4_out);
  and and_4 (_3, l, KEY[0], KEY[1], not_3_out, not_4_out);
  and and_5 (_4, l, not_1_out, not_2_out, KEY[2], not_4_out);
  and and_6 (_5, l, KEY[0], not_2_out, KEY[2], not_4_out);
  and and_7 (_6, l, not_1_out, KEY[1], KEY[2], not_4_out);
  and and_8 (_7, l, KEY[0], KEY[1], KEY[2], not_4_out);
  and and_9 (_8, l, not_1_out, not_2_out, not_3_out, KEY[3]);
  and and_10 (_9, l, KEY[0], not_2_out, not_3_out, KEY[3]);
  and and_11 (_10, l, not_1_out, KEY[1], not_3_out, KEY[3]);
  and and_12 (_11, l, KEY[0], KEY[1], not_3_out, KEY[3]);
  and and_13 (_12, l, not_1_out, not_2_out, KEY[2], KEY[3]);
  and and_14 (_13, l, KEY[0], not_2_out, KEY[2], KEY[3]);
  and and_15 (_14, l, not_1_out, KEY[1], KEY[2], KEY[3]);
  and and_16 (_15, l, KEY[0], KEY[1], KEY[2], KEY[3]);
endmodule

module MULT_2X1bit (
  input  in_1,
  input  in_2,
  input  in_3,
  output out_4
);

  wire and_1_out, and_2_out, not_1_out;

  not not_1 (not_1_out, in_3);
  and and_1 (and_1_out, in_1, not_1_out);
  and and_2 (and_2_out, in_2, in_3);
  or or_1 (out_4, and_1_out, and_2_out);
endmodule

module MULT_2X1_8bits (
  input  [7:0] entrada,
  input  chave,
  input  [7:0] entrada_2,
  output [7:0] out_4
);

  MULT_2X1bit mult_2x1bit_1 (.in_1(entrada[0]), .in_2(entrada_2[0]), .in_3(chave), .out_4(out_4[0]));
  MULT_2X1bit mult_2x1bit_2 (.in_1(entrada[1]), .in_2(entrada_2[1]), .in_3(chave), .out_4(out_4[1]));
  MULT_2X1bit mult_2x1bit_3 (.in_1(entrada[2]), .in_2(entrada_2[2]), .in_3(chave), .out_4(out_4[2]));
  MULT_2X1bit mult_2x1bit_4 (.in_1(entrada[3]), .in_2(entrada_2[3]), .in_3(chave), .out_4(out_4[3]));
  MULT_2X1bit mult_2x1bit_5 (.in_1(entrada[4]), .in_2(entrada_2[4]), .in_3(chave), .out_4(out_4[4]));
  MULT_2X1bit mult_2x1bit_6 (.in_1(entrada[5]), .in_2(entrada_2[5]), .in_3(chave), .out_4(out_4[5]));
  MULT_2X1bit mult_2x1bit_7 (.in_1(entrada[6]), .in_2(entrada_2[6]), .in_3(chave), .out_4(out_4[6]));
  MULT_2X1bit mult_2x1bit_8 (.in_1(entrada[7]), .in_2(entrada_2[7]), .in_3(chave), .out_4(out_4[7]));
endmodule

module MULT_16X1 (
  input  [7:0] _0,
  input  [7:0] _1,
  input  [7:0] _2,
  input  [7:0] _3,
  input  [7:0] _4,
  input  [7:0] _5,
  input  [7:0] _6,
  input  [7:0] _7,
  input  [7:0] _8,
  input  [7:0] _9,
  input  [7:0] _10,
  input  [7:0] _11,
  input  [7:0] _12,
  input  [7:0] _13,
  input  [7:0] _14,
  input  [7:0] _15,
  input  S,
  input  [3:0] CHAVE,
  output [7:0] \SAÍDA 
);

  wire and_1_out, and_2_out, and_3_out, and_4_out;
  wire [7:0] mult_2x1_8bits_1_out_4, mult_2x1_8bits_2_out_4, mult_2x1_8bits_3_out_4, mult_2x1_8bits_4_out_4,
       mult_2x1_8bits_5_out_4, mult_2x1_8bits_6_out_4, mult_2x1_8bits_7_out_4, mult_2x1_8bits_8_out_4,
       mult_2x1_8bits_9_out_4, mult_2x1_8bits_10_out_4, mult_2x1_8bits_11_out_4, mult_2x1_8bits_12_out_4,
       mult_2x1_8bits_13_out_4, mult_2x1_8bits_15_out_4;

  MULT_2X1_8bits mult_2x1_8bits_1 (.entrada(_0), .entrada_2(_1), .out_4(mult_2x1_8bits_1_out_4), .chave(and_1_out));
  MULT_2X1_8bits mult_2x1_8bits_2 (.entrada(_2), .entrada_2(_3), .out_4(mult_2x1_8bits_2_out_4), .chave(and_1_out));
  MULT_2X1_8bits mult_2x1_8bits_3 (.entrada(_4), .entrada_2(_5), .out_4(mult_2x1_8bits_3_out_4), .chave(and_1_out));
  MULT_2X1_8bits mult_2x1_8bits_4 (.entrada(_6), .entrada_2(_7), .out_4(mult_2x1_8bits_4_out_4), .chave(and_1_out));
  MULT_2X1_8bits mult_2x1_8bits_5 (.entrada(_8), .entrada_2(_9), .out_4(mult_2x1_8bits_5_out_4), .chave(and_1_out));
  MULT_2X1_8bits mult_2x1_8bits_6 (.entrada(_10), .entrada_2(_11), .out_4(mult_2x1_8bits_6_out_4), .chave(and_1_out));
  MULT_2X1_8bits mult_2x1_8bits_7 (.entrada(_12), .entrada_2(_13), .out_4(mult_2x1_8bits_7_out_4), .chave(and_1_out));
  MULT_2X1_8bits mult_2x1_8bits_8 (.entrada(_14), .entrada_2(_15), .out_4(mult_2x1_8bits_8_out_4), .chave(and_1_out));
  and and_1 (and_1_out, CHAVE[0], S);
  MULT_2X1_8bits mult_2x1_8bits_9 (
    .entrada(mult_2x1_8bits_1_out_4), .entrada_2(mult_2x1_8bits_2_out_4), .out_4(mult_2x1_8bits_9_out_4),
    .chave(and_2_out));
  MULT_2X1_8bits mult_2x1_8bits_10 (
    .entrada(mult_2x1_8bits_3_out_4), .entrada_2(mult_2x1_8bits_4_out_4), .out_4(mult_2x1_8bits_10_out_4),
    .chave(and_2_out));
  MULT_2X1_8bits mult_2x1_8bits_11 (
    .entrada(mult_2x1_8bits_5_out_4), .entrada_2(mult_2x1_8bits_6_out_4), .out_4(mult_2x1_8bits_11_out_4),
    .chave(and_2_out));
  MULT_2X1_8bits mult_2x1_8bits_12 (
    .entrada(mult_2x1_8bits_7_out_4), .entrada_2(mult_2x1_8bits_8_out_4), .out_4(mult_2x1_8bits_12_out_4),
    .chave(and_2_out));
  and and_2 (and_2_out, CHAVE[1], S);
  and and_3 (and_3_out, CHAVE[2], S);
  MULT_2X1_8bits mult_2x1_8bits_13 (
    .entrada(mult_2x1_8bits_9_out_4), .entrada_2(mult_2x1_8bits_10_out_4), .out_4(mult_2x1_8bits_13_out_4),
    .chave(and_3_out));
  MULT_2X1_8bits mult_2x1_8bits_14 (
    .entrada(mult_2x1_8bits_13_out_4), .entrada_2(mult_2x1_8bits_15_out_4), .out_4(\SAÍDA ), .chave(and_4_out));
  MULT_2X1_8bits mult_2x1_8bits_15 (
    .entrada(mult_2x1_8bits_11_out_4), .entrada_2(mult_2x1_8bits_12_out_4), .out_4(mult_2x1_8bits_15_out_4),
    .chave(and_3_out));
  and and_4 (and_4_out, CHAVE[3], S);
endmodule
