// Logisim project Contador Sincrono.circ as structural Verilog: 4 circuits, main circuit FlipFlop SR
module ContadorSincrono (
  input  Ligar,
  output [3:0] Contador
);

  wire and_1_out, and_2_out, Clock_out, flipflopd_1_q_prime, xor_1_out, xor_2_out, xor_3_out;

  Clock Clock (.out(Clock_out));
  xor xor_1 (xor_1_out, Contador[0], Contador[1]);
  flipflopD flipflopd_1 (
    .D(flipflopd_1_q_prime), .Clock(Clock_out), .Q(Contador[0]), .Q_prime(flipflopd_1_q_prime), .ligar(Ligar));
  flipflopD flipflopd_2 (.D(xor_1_out), .Clock(Clock_out), .Q(Contador[1]), .ligar(Ligar));  // open: Q_prime
  and and_1 (and_1_out, Contador[0], Contador[1]);
  xor xor_2 (xor_2_out, and_1_out, Contador[2]);
  flipflopD flipflopd_3 (.D(xor_2_out), .Clock(Clock_out), .Q(Contador[2]), .ligar(Ligar));  // open: Q_prime
  and and_2 (and_2_out, Contador[0], Contador[1], Contador[2]);
  xor xor_3 (xor_3_out, and_2_out, Contador[3]);
  flipflopD flipflopd_4 (.D(xor_3_out), .Clock(Clock_out), .Q(Contador[3]), .ligar(Ligar));  // open: Q_prime
endmodule

module FlipFlopJk (
  input  J,
  input  Clock,
  input  K,
  output out_4,
  output out_5
);

  wire and_1_out, and_2_out, not_1_out, or_1_out;

  and and_1 (and_1_out, out_5, J);
  not not_1 (not_1_out, K);
  and and_2 (and_2_out, not_1_out, out_4);
  or or_1 (or_1_out, and_1_out, and_2_out);
  flipflopD flipflopd_1 (.D(or_1_out), .Clock(Clock), .Q(out_4), .Q_prime(out_5));  // open: ligar
endmodule

module flipflopD (
  input  D,
  input  ligar,
  input  Clock,
  output Q,
  output Q_prime
);

  wire and_1_out, flipflop_sr_1_out_3, nand_1_out, nand_2_out, nand_3_out, nand_4_out, not_1_out, not_2_out,
       not_3_out;

  and and_1 (and_1_out, D, ligar);
  not not_1 (not_1_out, and_1_out);
  nand nand_1 (nand_1_out, and_1_out, Clock);
  nand nand_2 (nand_2_out, Clock, not_1_out);
  FlipFlop_SR flipflop_sr_1 (.in_1(nand_1_out), .in_2(nand_2_out), .out_3(flipflop_sr_1_out_3));  // open: out_4
  not not_2 (not_2_out, flipflop_sr_1_out_3);
  not not_3 (not_3_out, Clock);
  nand nand_3 (nand_3_out, flipflop_sr_1_out_3, not_3_out);
  nand nand_4 (nand_4_out, not_3_out, not_2_out);
  FlipFlop_SR flipflop_sr_2 (.in_1(nand_3_out), .in_2(nand_4_out), .out_3(Q), .out_4(Q_prime));
endmodule

module FlipFlop_SR (
  input  in_1,
  input  in_2,
  output out_3,
  output out_4
);

  nand nand_1 (out_3, in_1, out_4);
  nand nand_2 (out_4, out_3, in_2);
endmodule
