// Logisim project Decodificador de 7Segementos.circ as structural Verilog: 1 circuit, main circuit main
module main (
  input  D,
  input  C,
  input  B,
  input  A
);

  wire A_out, and_1_out, and_2_out, and_3_out, and_4_out, and_5_out, and_6_out, and_7_out, and_8_out,
       and_9_out, and_10_out, and_11_out, and_12_out, and_13_out, and_14_out, and_15_out, and_16_out,
       and_17_out, and_18_out, and_19_out, and_20_out, and_21_out, and_22_out, and_23_out, and_24_out,
       and_25_out, and_26_out, and_27_out, and_28_out, and_29_out, and_30_out, and_31_out, and_32_out,
       and_33_out, and_34_out, and_35_out, and_36_out, and_37_out, B_out, C_out, D_out, E_out, F_out, G_out,
       not_1_out, not_2_out, not_3_out, not_4_out, not_5_out, not_6_out, not_7_out, not_8_out, not_9_out,
       not_10_out, not_11_out, not_12_out, not_13_out, not_14_out, not_15_out, not_16_out, not_17_out,
       not_18_out, not_19_out, not_20_out, not_21_out, not_22_out, not_23_out, not_24_out, not_25_out,
       not_26_out, not_27_out, not_28_out, not_29_out, not_30_out, not_31_out, not_32_out, not_33_out,
       not_34_out, not_35_out, not_36_out, not_37_out, not_38_out, not_39_out, not_40_out, not_41_out,
       not_42_out, not_43_out, not_44_out, not_45_out, not_46_out, not_47_out;

  not not_1 (not_1_out, C);
  not not_2 (not_2_out, A);
  not not_3 (not_3_out, D);
  not not_4 (not_4_out, D);
  not not_5 (not_5_out, C);
  not not_6 (not_6_out, B);
  not not_7 (not_7_out, A);
  not not_8 (not_8_out, D);
  not not_9 (not_9_out, C);
  not not_10 (not_10_out, D);
  not not_11 (not_11_out, B);
  not not_12 (not_12_out, A);
  not not_13 (not_13_out, C);
  not not_14 (not_14_out, B);
  not not_15 (not_15_out, C);
  not not_16 (not_16_out, A);
  not not_17 (not_17_out, D);
  not not_18 (not_18_out, B);
  not not_19 (not_19_out, D);
  not not_20 (not_20_out, B);
  not not_21 (not_21_out, D);
  not not_22 (not_22_out, B);
  not not_23 (not_23_out, D);
  not not_24 (not_24_out, C);
  not not_25 (not_25_out, D);
  not not_26 (not_26_out, C);
  not not_27 (not_27_out, A);
  not not_28 (not_28_out, C);
  not not_29 (not_29_out, B);
  not not_30 (not_30_out, A);
  not not_31 (not_31_out, B);
  not not_32 (not_32_out, C);
  not not_33 (not_33_out, A);
  not not_34 (not_34_out, A);
  not not_35 (not_35_out, C);
  not not_36 (not_36_out, B);
  not not_37 (not_37_out, A);
  not not_38 (not_38_out, D);
  not not_39 (not_39_out, B);
  not not_40 (not_40_out, A);
  not not_41 (not_41_out, C);
  not not_42 (not_42_out, A);
  not not_43 (not_43_out, C);
  not not_44 (not_44_out, A);
  not not_45 (not_45_out, D);
  not not_46 (not_46_out, B);
  not not_47 (not_47_out, C);
  and and_1 (and_1_out, not_1_out, not_2_out);
  and and_2 (and_2_out, not_3_out, B);
  and and_3 (and_3_out, not_4_out, C, A);
  and and_4 (and_4_out, C, B);
  and and_5 (and_5_out, D, not_5_out, not_6_out);
  and and_6 (and_6_out, D, not_7_out);
  and and_7 (and_7_out, not_8_out, not_9_out);
  and and_8 (and_8_out, not_10_out, not_11_out, not_12_out);
  and and_9 (and_9_out, not_13_out, not_14_out);
  and and_10 (and_10_out, not_15_out, not_16_out);
  and and_11 (and_11_out, not_17_out, B, A);
  and and_12 (and_12_out, D, not_18_out, A);
  and and_13 (and_13_out, not_19_out, not_20_out);
  and and_14 (and_14_out, not_21_out, A);
  and and_15 (and_15_out, not_22_out, A);
  and and_16 (and_16_out, not_23_out, C);
  and and_17 (and_17_out, D, not_24_out);
  and and_18 (and_18_out, not_25_out, not_26_out, not_27_out);
  and and_19 (and_19_out, not_28_out, B, A);
  and and_20 (and_20_out, C, not_29_out, A);
  and and_21 (and_21_out, C, B, not_30_out);
  and and_22 (and_22_out, D, not_31_out);
  and and_23 (and_23_out, not_32_out, not_33_out);
  and and_24 (and_24_out, B, not_34_out);
  and and_25 (and_25_out, D, B);
  and and_26 (and_26_out, D, C);
  and and_27 (and_27_out, not_35_out, not_36_out, not_37_out);
  and and_28 (and_28_out, not_38_out, C, not_39_out, A);
  and and_29 (and_29_out, C, not_40_out);
  and and_30 (and_30_out, D, not_41_out);
  and and_31 (and_31_out, D, not_42_out);
  and and_32 (and_32_out, D, B);
  and and_33 (and_33_out, not_43_out, B);
  and and_34 (and_34_out, B, not_44_out);
  and and_35 (and_35_out, not_45_out, C, not_46_out);
  and and_36 (and_36_out, D, not_47_out);
  and and_37 (and_37_out, D, A);
  or u_A (A_out, and_1_out, and_2_out, and_3_out, and_4_out, and_5_out, and_6_out);
  or u_B (B_out, and_7_out, and_8_out, and_9_out, and_10_out, and_11_out, and_12_out);
  or u_C (C_out, and_13_out, and_14_out, and_15_out, and_16_out, and_17_out);
  or u_D (D_out, and_18_out, and_19_out, and_20_out, and_21_out, and_22_out);
  or E (E_out, and_23_out, and_24_out, and_25_out, and_26_out);
  or F (F_out, and_27_out, and_28_out, and_29_out, and_30_out, and_31_out, and_32_out);
  or G (G_out, and_33_out, and_34_out, and_35_out, and_36_out, and_37_out);
  _7_Segment_Display u_7_segment_display_1 (
    .g(G_out), .f(F_out), .a(A_out), .b(B_out), .e(E_out), .d(D_out), .c(C_out));  // open: dp

  // Notes on the sheet:
  //   portas superiores:
  //   portas inferiores:
  //   Display de 7 segmentos
  //   G / F / A / B
  //   E / D / C / DP
endmodule
