// Logisim project Detector de 101.circ as structural Verilog: 1 circuit, main circuit Detector 101
module Detector_101 (
  input  [7:0] ENTRADA,
  output \SAÍDA 
);

  wire and_1_out, and_2_out, and_3_out, and_4_out, and_5_out, and_6_out, and_7_out;

  and and_1 (and_1_out, ENTRADA[0], ~ENTRADA[1], ENTRADA[2]);  // AND_Gate
  and and_2 (and_2_out, ENTRADA[1], ~ENTRADA[2], ENTRADA[3]);  // AND_Gate
  and and_3 (and_3_out, ENTRADA[2], ~ENTRADA[3], ENTRADA[4]);  // AND_Gate
  and and_4 (and_4_out, ENTRADA[3], ~ENTRADA[4], ENTRADA[5]);  // AND_Gate
  and and_5 (and_5_out, ENTRADA[4], ~ENTRADA[5], ENTRADA[6]);  // AND_Gate
  and and_6 (and_6_out, ENTRADA[5], ~ENTRADA[6], ENTRADA[7]);  // AND_Gate
  and and_7 (and_7_out, ENTRADA[6], ~ENTRADA[7], ENTRADA[7]);  // AND_Gate
  or or_1 (\SAÍDA , and_1_out, and_2_out, and_3_out, and_4_out, and_5_out, and_6_out, and_7_out);
endmodule
