// Logisim project Detector de Paridadde Impar.circ as structural Verilog: 1 circuit, main circuit Detector de paridade impar
module Detector_de_paridade_impar (
  input  [3:0] ENTRADA,
  output out_2
);

  wire and_1_out, and_2_out, and_3_out, and_4_out, and_5_out, and_6_out, and_7_out, and_8_out;

  and and_1 (and_1_out, ENTRADA[3], ~ENTRADA[2], ~ENTRADA[1], ~ENTRADA[0]);  // AND_Gate
  and and_2 (and_2_out, ~ENTRADA[3], ENTRADA[2], ~ENTRADA[1], ~ENTRADA[0]);  // AND_Gate
  and and_3 (and_3_out, ~ENTRADA[3], ~ENTRADA[2], ENTRADA[1], ~ENTRADA[0]);  // AND_Gate
  and and_4 (and_4_out, ~ENTRADA[3], ~ENTRADA[2], ~ENTRADA[1], ENTRADA[0]);  // AND_Gate
  and and_5 (and_5_out, ENTRADA[3], ENTRADA[2], ENTRADA[1], ~ENTRADA[0]);  // AND_Gate
  and and_6 (and_6_out, ENTRADA[3], ENTRADA[2], ~ENTRADA[1], ENTRADA[0]);  // AND_Gate
  and and_7 (and_7_out, ENTRADA[3], ~ENTRADA[2], ENTRADA[1], ENTRADA[0]);  // AND_Gate
  and and_8 (and_8_out, ~ENTRADA[3], ENTRADA[2], ENTRADA[1], ENTRADA[0]);  // AND_Gate
  or or_1 (out_2, and_1_out, and_2_out, and_3_out, and_4_out, and_5_out, and_6_out, and_7_out, and_8_out);
endmodule
