// Logisim project Detector de minoria.circ as structural Verilog: 1 circuit, main circuit detector de minoria
module detector_de_minoria (
  input  A,
  input  B,
  input  C,
  output out_4
);

  wire and_1_out, and_2_out, and_3_out, not_1_out, not_2_out, not_3_out;

  not not_1 (not_1_out, A);
  not not_2 (not_2_out, B);
  not not_3 (not_3_out, C);
  and and_1 (and_1_out, not_1_out, not_2_out);
  and and_2 (and_2_out, not_1_out, not_3_out);
  and and_3 (and_3_out, not_2_out, not_3_out);
  or or_1 (out_4, and_1_out, and_2_out, and_3_out);
endmodule
