// Logisim project Flip-Flops D e JK.circ as structural Verilog: 1 circuit, main circuit Flip-Flops D e JK
module Flip_Flops_D_e_JK (
  input  in_1,
  input  in_2,
  input  in_3,
  output out_4,
  output out_5,
  output out_6,
  output out_7
);

  wire clock_1_out, clock_2_out, nand_1_out, nand_2_out, nand_3_out, nand_4_out, nand_7_out, nand_8_out,
       nand_9_out, nand_10_out, not_1_out, not_2_out, not_3_out;

  Clock clock_1 (.out(clock_1_out));
  Clock clock_2 (.out(clock_2_out));
  not not_1 (not_1_out, clock_1_out);
  not not_2 (not_2_out, in_1);
  nand nand_1 (nand_1_out, in_1, clock_2_out);
  nand nand_2 (nand_2_out, not_2_out, clock_2_out);
  nand nand_3 (nand_3_out, out_7, in_2, not_1_out);
  nand nand_4 (nand_4_out, not_1_out, in_3, out_6);
  nand nand_5 (out_4, nand_1_out, out_5);
  nand nand_6 (out_5, out_4, nand_2_out);
  nand nand_7 (nand_7_out, nand_3_out, nand_8_out);
  nand nand_8 (nand_8_out, nand_7_out, nand_4_out);
  not not_3 (not_3_out, not_1_out);
  nand nand_9 (nand_9_out, nand_7_out, not_3_out);
  nand nand_10 (nand_10_out, not_3_out, nand_8_out);
  nand nand_11 (out_6, nand_9_out, out_7);
  nand nand_12 (out_7, out_6, nand_10_out);
endmodule
