// Logisim project MaquinaDeEstadosDef.circ as structural Verilog: 2 circuits, main circuit main
module main (
  input  X,
  input  Set,
  input  Reset,
  output X1,
  output X2
);

  wire and_1_out, and_2_out, Clock_out, flip_flop_d_1_q, flip_flop_d_2_q, not_1_out;

  Clock Clock (.out(Clock_out));
  and and_1 (and_1_out, X, X2);
  and and_2 (and_2_out, X, X1);
  flip_flop_d flip_flop_d_1 (
    .SET(Set), .Q(flip_flop_d_1_q), .INPUT(and_1_out), .CLOCK(Clock_out), .RESET(Reset));  // open: nQ
  flip_flop_d flip_flop_d_2 (
    .SET(Set), .Q(flip_flop_d_2_q), .INPUT(and_2_out), .CLOCK(Clock_out), .RESET(Reset));  // open: nQ
  not not_1 (not_1_out, flip_flop_d_2_q);
  and and_3 (X1, X, flip_flop_d_1_q);
  and and_4 (X2, X, not_1_out);

  // Notes on the sheet:
  //   A = 00
  //   B = 01
  //   C = 10
  //   D = 11
endmodule

module flip_flop_d (
  input  SET,
  input  INPUT,
  input  CLOCK,
  input  RESET,
  output Q,
  output nQ
);

  wire nand_1_out, nand_2_out, nand_3_out, nand_4_out, nand_5_out, nand_6_out, not_1_out, not_2_out,
       not_3_out, not_4_out;

  not not_1 (not_1_out, INPUT);
  not not_2 (not_2_out, SET);
  nand nand_1 (nand_1_out, nQ, INPUT, CLOCK);
  nand nand_2 (nand_2_out, CLOCK, not_1_out, Q);
  not not_3 (not_3_out, RESET);
  nand nand_3 (nand_3_out, not_2_out, nand_1_out, nand_4_out);
  not not_4 (not_4_out, CLOCK);
  nand nand_4 (nand_4_out, nand_3_out, nand_2_out, not_3_out);
  nand nand_5 (nand_5_out, nand_3_out, not_3_out, not_4_out);
  nand nand_6 (nand_6_out, not_4_out, not_2_out, nand_4_out);
  nand nand_7 (Q, not_2_out, nand_5_out, nQ);
  nand nand_8 (nQ, Q, nand_6_out, not_3_out);
endmodule
