// Logisim project Memoria ROM 8 bits.circ as structural Verilog: 1 circuit, main circuit main
module main (
  input  C,
  input  B,
  input  A,
  output [7:0] out_4
);

  wire _0_out, _1_out, _2_out, _3_out, _4_out, _5_out, _6_out, _7_out, not_1_out, not_2_out, not_3_out;

  and _7 (_7_out, A, B, C);
  and _6 (_6_out, not_3_out, B, C);
  and _5 (_5_out, A, not_2_out, C);
  and _4 (_4_out, not_3_out, not_2_out, C);
  and _3 (_3_out, A, B, not_1_out);
  and _2 (_2_out, not_3_out, B, not_1_out);
  and _1 (_1_out, A, not_2_out, not_1_out);
  not not_1 (not_1_out, C);
  not not_2 (not_2_out, B);
  not not_3 (not_3_out, A);
  and _0 (_0_out, not_3_out, not_2_out, not_1_out);
  or or_1 (out_4[0], _6_out, _5_out, _4_out, _2_out);
  or or_2 (out_4[1], _4_out, _2_out, _1_out, _0_out);
  or or_3 (out_4[2], _6_out, _5_out, _3_out, _2_out);
  or or_4 (out_4[3], _7_out, _3_out, _1_out, _0_out);
  or or_5 (out_4[4], _7_out, _5_out, _3_out, _1_out);
  or or_6 (out_4[5], _6_out, _4_out, _2_out, _1_out);
  or or_7 (out_4[6], _7_out, _4_out, _2_out, _0_out);
  or or_8 (out_4[7], _4_out, _3_out, _1_out, _0_out);
endmodule
