// Logisim project Memória RAM 8Bits.circ as structural Verilog: 6 circuits, main circuit Memória RAM
module \Memória_RAM  (
  input  in_1,
  input  in_2,
  input  in_3,
  input  Set,
  input  [7:0] I,
  input  [2:0] in_6,
  input  Set_2,
  output [7:0] LEITURA
);

  wire _0_out, _1_out, _2_out, _3_out, _4_out, _5_out, _6_out, _7_out, and_1_out, and_2_out, and_3_out,
       and_4_out, and_5_out, and_6_out, and_7_out, and_8_out, not_1_out, not_2_out, not_3_out, not_4_out,
       not_5_out, not_6_out, not_7_out, not_8_out, not_9_out, not_10_out, not_11_out, not_12_out;
  wire [7:0] registrador_1_saida, registrador_2_saida, registrador_3_saida, registrador_4_saida,
       registrador_5_saida, registrador_6_saida, registrador_7_saida, registrador_8_saida;

  not not_1 (not_1_out, in_1);
  not not_2 (not_2_out, in_2);
  and _0 (_0_out, not_1_out, not_2_out, not_4_out);
  not not_3 (not_3_out, in_2);
  not not_4 (not_4_out, in_3);
  not not_5 (not_5_out, in_1);
  and _1 (_1_out, not_5_out, not_3_out, in_3);
  and and_1 (and_1_out, _0_out, Set);
  Registrador registrador_1 (.Entrada(I), .CLK(and_1_out), .Saida(registrador_1_saida));
  not not_6 (not_6_out, in_1);
  and _2 (_2_out, not_6_out, in_2, not_8_out);
  and and_2 (and_2_out, _1_out, Set);
  Registrador registrador_2 (.Entrada(I), .CLK(and_2_out), .Saida(registrador_2_saida));
  not not_7 (not_7_out, in_1);
  not not_8 (not_8_out, in_3);
  and _3 (_3_out, not_7_out, in_2, in_3);
  and and_3 (and_3_out, _2_out, Set);
  Registrador registrador_3 (.Entrada(I), .CLK(and_3_out), .Saida(registrador_3_saida));
  not not_9 (not_9_out, in_2);
  and _4 (_4_out, in_1, not_9_out, not_10_out);
  and and_4 (and_4_out, _3_out, Set);
  Registrador registrador_4 (.Entrada(I), .CLK(and_4_out), .Saida(registrador_4_saida));
  Multiplexador_8x1 multiplexador_8x1_1 (
    ._1(registrador_2_saida), ._2(registrador_3_saida), ._3(registrador_4_saida), ._4(registrador_5_saida),
    ._5(registrador_6_saida), ._6(registrador_7_saida), ._7(registrador_8_saida), .chave(in_6),
    .saida(LEITURA), .S(Set_2), ._0(registrador_1_saida));
  not not_10 (not_10_out, in_3);
  not not_11 (not_11_out, in_2);
  and _5 (_5_out, in_1, not_11_out, in_3);
  and and_5 (and_5_out, _4_out, Set);
  Registrador registrador_5 (.Entrada(I), .CLK(and_5_out), .Saida(registrador_5_saida));
  and _6 (_6_out, in_1, in_2, not_12_out);
  and and_6 (and_6_out, _5_out, Set);
  Registrador registrador_6 (.Entrada(I), .CLK(and_6_out), .Saida(registrador_6_saida));
  not not_12 (not_12_out, in_3);
  and _7 (_7_out, in_3, in_2, in_1);
  and and_7 (and_7_out, _6_out, Set);
  Registrador registrador_7 (.Entrada(I), .CLK(and_7_out), .Saida(registrador_7_saida));
  and and_8 (and_8_out, _7_out, Set);
  Registrador registrador_8 (.Entrada(I), .CLK(and_8_out), .Saida(registrador_8_saida));

  // Notes on the sheet:
  //   ESCRITA
  //   Memória RAM
  //   DECODIFICADOR DE ENDEREÇOS
endmodule

module Flip_Flop_D (
  input  D,
  input  CLK,
  output Q,
  output Q_prime
);

  wire nand_1_out, nand_2_out, not_1_out;

  not not_1 (not_1_out, D);
  nand nand_1 (nand_1_out, D, CLK);
  nand nand_2 (nand_2_out, not_1_out, CLK);
  nand nand_3 (Q, nand_1_out, Q_prime);
  nand nand_4 (Q_prime, Q, nand_2_out);

  // Notes on the sheet:
  //   Flip-Flop  D
endmodule

module Registrador (
  input  [7:0] Entrada,
  input  CLK,
  output [7:0] Saida
);

  wire ff_d_7_q_prime;

  Flip_Flop_D ff_d_1 (.D(Entrada[7]), .Q(Saida[7]), .CLK(CLK));  // open: Q_prime
  Flip_Flop_D ff_d_2 (.D(Entrada[6]), .Q(Saida[6]), .CLK(CLK));  // open: Q_prime
  Flip_Flop_D ff_d_3 (.D(Entrada[5]), .Q(Saida[5]), .CLK(CLK));  // open: Q_prime
  Flip_Flop_D ff_d_4 (.D(Entrada[4]), .Q(Saida[4]), .CLK(CLK));  // open: Q_prime
  Flip_Flop_D ff_d_5 (.D(Entrada[3]), .Q(Saida[3]), .CLK(CLK));  // open: Q_prime
  Flip_Flop_D ff_d_6 (.D(Entrada[2]), .Q(Saida[2]), .CLK(CLK));  // open: Q_prime
  Flip_Flop_D ff_d_7 (.D(Entrada[1]), .Q(Saida[1]), .Q_prime(ff_d_7_q_prime), .CLK(CLK));
  Flip_Flop_D ff_d_8 (.D(Entrada[0]), .Q(Saida[0]), .CLK(CLK));  // open: Q_prime

  // Notes on the sheet:
  //   Registrador de 8 bits
endmodule

module Multiplexador_2X1 (
  input  Entradas,
  input  Entradas_2,
  input  Entradas_3,
  output Saida
);

  wire and_1_out, and_2_out;

  and and_1 (and_1_out, Entradas, ~Entradas_3);  // AND_Gate
  and and_2 (and_2_out, Entradas_2, Entradas_3);
  or or_1 (Saida, and_1_out, and_2_out);
endmodule

module Multiplexador_2x1_8Bits (
  input  [7:0] Entrada,
  input  [7:0] Entrada_2,
  input  Chave,
  output [7:0] Saida
);

  Multiplexador_2X1 multiplexador_2x1_1 (
    .Entradas(Entrada[0]), .Entradas_2(Entrada_2[0]), .Entradas_3(Chave), .Saida(Saida[0]));
  Multiplexador_2X1 multiplexador_2x1_2 (
    .Entradas(Entrada[1]), .Entradas_2(Entrada_2[1]), .Entradas_3(Chave), .Saida(Saida[1]));
  Multiplexador_2X1 multiplexador_2x1_3 (
    .Entradas(Entrada[2]), .Entradas_2(Entrada_2[2]), .Entradas_3(Chave), .Saida(Saida[2]));
  Multiplexador_2X1 multiplexador_2x1_4 (
    .Entradas(Entrada[3]), .Entradas_2(Entrada_2[3]), .Entradas_3(Chave), .Saida(Saida[3]));
  Multiplexador_2X1 multiplexador_2x1_5 (
    .Entradas(Entrada[4]), .Entradas_2(Entrada_2[4]), .Entradas_3(Chave), .Saida(Saida[4]));
  Multiplexador_2X1 multiplexador_2x1_6 (
    .Entradas(Entrada[5]), .Entradas_2(Entrada_2[5]), .Entradas_3(Chave), .Saida(Saida[5]));
  Multiplexador_2X1 multiplexador_2x1_7 (
    .Entradas(Entrada[6]), .Entradas_2(Entrada_2[6]), .Entradas_3(Chave), .Saida(Saida[6]));
  Multiplexador_2X1 multiplexador_2x1_8 (
    .Entradas(Entrada[7]), .Entradas_2(Entrada_2[7]), .Entradas_3(Chave), .Saida(Saida[7]));
endmodule

module Multiplexador_8x1 (
  input  [7:0] _0,
  input  [7:0] _1,
  input  [7:0] _2,
  input  [7:0] _3,
  input  [7:0] _4,
  input  [7:0] _5,
  input  [7:0] _6,
  input  [7:0] _7,
  input  S,
  input  [2:0] chave,
  output [7:0] saida
);

  wire and_1_out, and_2_out, and_3_out;
  wire [7:0] multiplexador_2x1_8bits_1_saida, multiplexador_2x1_8bits_2_saida,
       multiplexador_2x1_8bits_3_saida, multiplexador_2x1_8bits_4_saida, multiplexador_2x1_8bits_5_saida,
       multiplexador_2x1_8bits_6_saida;

  Multiplexador_2x1_8Bits multiplexador_2x1_8bits_1 (
    .Entrada(_0), .Entrada_2(_1), .Saida(multiplexador_2x1_8bits_1_saida), .Chave(and_2_out));
  Multiplexador_2x1_8Bits multiplexador_2x1_8bits_2 (
    .Entrada(_2), .Entrada_2(_3), .Saida(multiplexador_2x1_8bits_2_saida), .Chave(and_2_out));
  Multiplexador_2x1_8Bits multiplexador_2x1_8bits_3 (
    .Entrada(_4), .Entrada_2(_5), .Saida(multiplexador_2x1_8bits_3_saida), .Chave(and_2_out));
  Multiplexador_2x1_8Bits multiplexador_2x1_8bits_4 (
    .Entrada(_6), .Entrada_2(_7), .Saida(multiplexador_2x1_8bits_4_saida), .Chave(and_2_out));
  and and_1 (and_1_out, chave[1], S);
  and and_2 (and_2_out, chave[0], S);
  Multiplexador_2x1_8Bits multiplexador_2x1_8bits_5 (
    .Entrada(multiplexador_2x1_8bits_1_saida), .Entrada_2(multiplexador_2x1_8bits_2_saida),
    .Saida(multiplexador_2x1_8bits_5_saida), .Chave(and_1_out));
  Multiplexador_2x1_8Bits multiplexador_2x1_8bits_6 (
    .Entrada(multiplexador_2x1_8bits_3_saida), .Entrada_2(multiplexador_2x1_8bits_4_saida),
    .Saida(multiplexador_2x1_8bits_6_saida), .Chave(and_1_out));
  and and_3 (and_3_out, chave[2], S);
  Multiplexador_2x1_8Bits multiplexador_2x1_8bits_7 (
    .Entrada(multiplexador_2x1_8bits_5_saida), .Entrada_2(multiplexador_2x1_8bits_6_saida), .Saida(saida),
    .Chave(and_3_out));
endmodule
