// Logisim project ULA.circ as structural Verilog: 12 circuits, main circuit Somador 8bits
module ULA (
  input  [7:0] in_1,
  input  [7:0] in_2,
  input  [3:0] Seletor,
  output [7:0] out_4,
  output out_5,
  output out_6
);

  wire [7:0] and_1_out, nand_1_out, nor_1_out, not_1_out, not_2_out, or_1_out, shift_direita_1_out_2,
       shift_direita_2_out_2, shift_esquerda_1_saida, shift_esquerda_2_saida, somador_8bits_1_out_3,
       subtrator_8bits_1_out_3, xor_1_out;

  assign not_1_out = ~in_1;  // NOT_Gate not_1, 8 bits wide
  assign not_2_out = ~in_2;  // NOT_Gate not_2, 8 bits wide
  assign and_1_out = in_1 & in_2;  // AND_Gate and_1, 8 bits wide
  assign or_1_out = in_1 | in_2;  // OR_Gate or_1, 8 bits wide
  assign nor_1_out = ~(in_1 | in_2);  // NOR_Gate nor_1, 8 bits wide
  assign nand_1_out = ~(in_1 & in_2);  // NAND_Gate nand_1, 8 bits wide
  assign xor_1_out = in_1 ^ in_2;  // XOR_Gate xor_1, 8 bits wide
  Shift_Esquerda shift_esquerda_1 (.in_1(in_1), .Saida(shift_esquerda_1_saida));
  Shift_Esquerda shift_esquerda_2 (.in_1(in_2), .Saida(shift_esquerda_2_saida));
  Shift_Direita shift_direita_1 (.A_B(in_1), .out_2(shift_direita_1_out_2));
  Shift_Direita shift_direita_2 (.A_B(in_2), .out_2(shift_direita_2_out_2));
  Somador_8bits somador_8bits_1 (.out_3(somador_8bits_1_out_3), .A(in_1), .B(in_2), .Carry_out(out_5));
  Subtrator_8bits subtrator_8bits_1 (
    .out_3(subtrator_8bits_1_out_3), .Entrada_A(in_1), .Entrada_B(in_2), .Carry_out(out_6));
  Mult_16x1x8 mult_16x1x8_1 (
    .in_1(and_1_out), .in_2(or_1_out), .in_3(not_1_out), .in_4(not_2_out), .in_5(nor_1_out),
    .in_6(nand_1_out), .in_7(xor_1_out), .in_8(shift_esquerda_1_saida), .in_9(shift_esquerda_2_saida),
    .in_10(shift_direita_1_out_2), .in_11(shift_direita_2_out_2), .in_12(somador_8bits_1_out_3),
    .in_13(subtrator_8bits_1_out_3), .Select(Seletor), .out_15(out_4));

  // Notes on the sheet:
  //   A
  //   B
endmodule

module Somador_8bits (
  input  [7:0] A,
  input  [7:0] B,
  output [7:0] out_3,
  output Carry_out
);

  wire somador_1bit_1_carry_out, somador_1bit_2_carry_out, somador_1bit_3_carry_out,
       somador_1bit_4_carry_out, somador_1bit_5_carry_out, somador_1bit_6_carry_out, somador_1bit_7_carry_out;

  Somador_1bit somador_1bit_1 (
    .Entrada_A(A[0]), .Entrada_B(B[0]), .Saida(out_3[0]), .Carry_out(somador_1bit_1_carry_out),
    .Carry_in(1'b0));
  Somador_1bit somador_1bit_2 (
    .Entrada_A(A[1]), .Entrada_B(B[1]), .Saida(out_3[1]), .Carry_out(somador_1bit_2_carry_out),
    .Carry_in(somador_1bit_1_carry_out));
  Somador_1bit somador_1bit_3 (
    .Entrada_A(A[2]), .Entrada_B(B[2]), .Saida(out_3[2]), .Carry_out(somador_1bit_3_carry_out),
    .Carry_in(somador_1bit_2_carry_out));
  Somador_1bit somador_1bit_4 (
    .Entrada_A(A[3]), .Entrada_B(B[3]), .Saida(out_3[3]), .Carry_out(somador_1bit_4_carry_out),
    .Carry_in(somador_1bit_3_carry_out));
  Somador_1bit somador_1bit_5 (
    .Entrada_A(A[4]), .Entrada_B(B[4]), .Saida(out_3[4]), .Carry_out(somador_1bit_5_carry_out),
    .Carry_in(somador_1bit_4_carry_out));
  Somador_1bit somador_1bit_6 (
    .Entrada_A(A[5]), .Entrada_B(B[5]), .Saida(out_3[5]), .Carry_out(somador_1bit_6_carry_out),
    .Carry_in(somador_1bit_5_carry_out));
  Somador_1bit somador_1bit_7 (
    .Entrada_A(A[6]), .Entrada_B(B[6]), .Saida(out_3[6]), .Carry_out(somador_1bit_7_carry_out),
    .Carry_in(somador_1bit_6_carry_out));
  Somador_1bit somador_1bit_8 (
    .Entrada_A(A[7]), .Entrada_B(B[7]), .Saida(out_3[7]), .Carry_out(Carry_out),
    .Carry_in(somador_1bit_7_carry_out));

  // Notes on the sheet:
  //   Carry in
  //   S
endmodule

module Subtrator_8bits (
  input  [7:0] Entrada_A,
  input  [7:0] Entrada_B,
  output [7:0] out_3,
  output Carry_out
);

  wire subtrator_1bit_1_carry_out, subtrator_1bit_2_carry_out, subtrator_1bit_3_carry_out,
       subtrator_1bit_4_carry_out, subtrator_1bit_5_carry_out, subtrator_1bit_6_carry_out,
       subtrator_1bit_7_carry_out, subtrator_1bit_8_carry_out;

  Subtrator_1bit subtrator_1bit_1 (
    .Entrada_A(Entrada_A[0]), .Entrada_B(Entrada_B[0]), .Saida(out_3[0]),
    .Carry_out(subtrator_1bit_1_carry_out));
  Subtrator_1bit subtrator_1bit_2 (
    .Entrada_A(Entrada_A[1]), .Entrada_B(Entrada_B[1]), .Saida(out_3[1]),
    .Carry_out(subtrator_1bit_2_carry_out));
  Subtrator_1bit subtrator_1bit_3 (
    .Entrada_A(Entrada_B[2]), .Entrada_B(Entrada_A[2]), .Saida(out_3[2]),
    .Carry_out(subtrator_1bit_3_carry_out));
  Subtrator_1bit subtrator_1bit_4 (
    .Entrada_A(Entrada_A[3]), .Entrada_B(Entrada_B[3]), .Saida(out_3[3]),
    .Carry_out(subtrator_1bit_4_carry_out));
  Subtrator_1bit subtrator_1bit_5 (
    .Entrada_A(Entrada_A[4]), .Entrada_B(Entrada_B[4]), .Saida(out_3[4]),
    .Carry_out(subtrator_1bit_5_carry_out));
  Subtrator_1bit subtrator_1bit_6 (
    .Entrada_A(Entrada_A[5]), .Entrada_B(Entrada_B[5]), .Saida(out_3[5]),
    .Carry_out(subtrator_1bit_6_carry_out));
  Subtrator_1bit subtrator_1bit_7 (
    .Entrada_A(Entrada_A[6]), .Entrada_B(Entrada_B[6]), .Saida(out_3[6]),
    .Carry_out(subtrator_1bit_7_carry_out));
  Subtrator_1bit subtrator_1bit_8 (
    .Entrada_A(Entrada_A[7]), .Entrada_B(Entrada_B[7]), .Saida(out_3[7]),
    .Carry_out(subtrator_1bit_8_carry_out));
  and and_1 (Carry_out, subtrator_1bit_1_carry_out, subtrator_1bit_2_carry_out, subtrator_1bit_3_carry_out, subtrator_1bit_4_carry_out, subtrator_1bit_5_carry_out, subtrator_1bit_6_carry_out, subtrator_1bit_7_carry_out, subtrator_1bit_8_carry_out);

  // Notes on the sheet:
  //   Saida
endmodule

module Somador_1bit (
  input  Carry_in,
  input  Entrada_A,
  input  Entrada_B,
  output Saida,
  output Carry_out
);

  wire and_1_out, and_2_out, and_3_out, xor_1_out;

  and and_1 (and_1_out, Entrada_A, Entrada_B);
  and and_2 (and_2_out, Carry_in, Entrada_A);
  and and_3 (and_3_out, Entrada_B, Carry_in);
  xor xor_1 (xor_1_out, Entrada_A, Entrada_B);
  or or_1 (Carry_out, and_1_out, and_2_out, and_3_out);
  xor xor_2 (Saida, xor_1_out, Carry_in);
endmodule

module Subtrator_1bit (
  input  Entrada_A,
  input  Entrada_B,
  output Saida,
  output Carry_out
);

  wire and_1_out, and_2_out, not_1_out, xor_1_out;

  not not_1 (not_1_out, Entrada_B);
  xor xor_1 (xor_1_out, Entrada_A, not_1_out);
  and and_1 (and_1_out, Entrada_A, not_1_out);
  xor xor_2 (Saida, 1'b1, xor_1_out);
  and and_2 (and_2_out, 1'b1, xor_1_out);
  or or_1 (Carry_out, and_2_out, and_1_out);
endmodule

module Shift_Esquerda (
  input  [7:0] in_1,
  output [7:0] Saida
);


  assign Saida = {in_1[5:0], 2'b00};

  // Notes on the sheet:
  //   A|B
endmodule

module Shift_Direita (
  input  [7:0] A_B,
  output [7:0] out_2
);


  assign out_2 = {2'b00, A_B[7:2]};

  // Notes on the sheet:
  //   Saida
endmodule

module Mult_2x1 (
  input  Entrada_A,
  input  Entrada_B,
  input  Select,
  output Saida
);

  wire and_1_out, and_2_out;

  and and_1 (and_1_out, Entrada_A, ~Select);  // AND_Gate
  and and_2 (and_2_out, Entrada_B, Select);
  or or_1 (Saida, and_1_out, and_2_out);
endmodule

module Mult_2x1x8 (
  input  [7:0] _0,
  input  [7:0] _1,
  input  in_3,
  output [7:0] out_4
);

  Mult_2x1 mult_2x1_1 (.Entrada_A(_0[0]), .Entrada_B(_1[0]), .Saida(out_4[0]), .Select(in_3));
  Mult_2x1 mult_2x1_2 (.Entrada_A(_0[1]), .Entrada_B(_1[1]), .Saida(out_4[1]), .Select(in_3));
  Mult_2x1 mult_2x1_3 (.Entrada_A(_0[2]), .Entrada_B(_1[2]), .Saida(out_4[2]), .Select(in_3));
  Mult_2x1 mult_2x1_4 (.Entrada_A(_0[3]), .Entrada_B(_1[3]), .Saida(out_4[3]), .Select(in_3));
  Mult_2x1 mult_2x1_5 (.Entrada_A(_0[4]), .Entrada_B(_1[4]), .Saida(out_4[4]), .Select(in_3));
  Mult_2x1 mult_2x1_6 (.Entrada_A(_0[5]), .Entrada_B(_1[5]), .Saida(out_4[5]), .Select(in_3));
  Mult_2x1 mult_2x1_7 (.Entrada_A(_0[6]), .Entrada_B(_1[6]), .Saida(out_4[6]), .Select(in_3));
  Mult_2x1 mult_2x1_8 (.Entrada_A(_0[7]), .Entrada_B(_1[7]), .Saida(out_4[7]), .Select(in_3));
endmodule

module Mult_4x1x8 (
  input  [7:0] in_1,
  input  [7:0] in_2,
  input  [7:0] in_3,
  input  [7:0] in_4,
  input  [1:0] Select,
  output [7:0] Saida
);

  wire [7:0] mult_2x1x8_1_out_4, mult_2x1x8_2_out_4;

  Mult_2x1x8 mult_2x1x8_1 (.out_4(mult_2x1x8_1_out_4), ._0(in_1), ._1(in_2), .in_3(Select[0]));
  Mult_2x1x8 mult_2x1x8_2 (.out_4(mult_2x1x8_2_out_4), ._0(in_3), ._1(in_4), .in_3(Select[0]));
  Mult_2x1x8 mult_2x1x8_3 (.out_4(Saida), ._0(mult_2x1x8_1_out_4), ._1(mult_2x1x8_2_out_4), .in_3(Select[1]));

  // Notes on the sheet:
  //   0
  //   1
  //   2
  //   3
endmodule

module Mult_8x1x8 (
  input  [7:0] in_1,
  input  [7:0] in_2,
  input  [7:0] in_3,
  input  [7:0] in_4,
  input  [7:0] in_5,
  input  [7:0] in_6,
  input  [7:0] in_7,
  input  [7:0] in_8,
  input  [2:0] Select,
  output [7:0] out_10
);

  wire [7:0] mult_4x1x8_1_saida, mult_4x1x8_2_saida;

  Mult_4x1x8 mult_4x1x8_1 (
    .in_3(in_3), .in_4(in_4), .Select(Select[1:0]), .Saida(mult_4x1x8_1_saida), .in_1(in_1), .in_2(in_2));
  Mult_4x1x8 mult_4x1x8_2 (
    .in_3(in_7), .in_4(in_8), .Select(Select[1:0]), .Saida(mult_4x1x8_2_saida), .in_1(in_5), .in_2(in_6));
  Mult_2x1x8 mult_2x1x8_1 (.out_4(out_10), ._0(mult_4x1x8_1_saida), ._1(mult_4x1x8_2_saida), .in_3(Select[2]));

  // Notes on the sheet:
  //   0
  //   1
  //   2
  //   3
  //   4
  //   5
  //   6
  //   7
  //   Saida
endmodule

module Mult_16x1x8 (
  input  [7:0] in_1,
  input  [7:0] in_2,
  input  [7:0] in_3,
  input  [7:0] in_4,
  input  [7:0] in_5,
  input  [7:0] in_6,
  input  [7:0] in_7,
  input  [7:0] in_8,
  input  [7:0] in_9,
  input  [7:0] in_10,
  input  [7:0] in_11,
  input  [7:0] in_12,
  input  [7:0] in_13,
  input  [3:0] Select,
  output [7:0] out_15
);

  wire [7:0] mult_8x1x8_1_out_10, mult_8x1x8_2_out_10;

  Mult_8x1x8 mult_8x1x8_1 (
    .in_1(in_1), .in_2(in_2), .in_3(in_3), .in_4(in_4), .in_5(in_5), .in_6(in_6), .in_7(in_7), .in_8(in_8),
    .Select(Select[2:0]), .out_10(mult_8x1x8_1_out_10));
  Mult_8x1x8 mult_8x1x8_2 (
    .in_1(in_9), .in_2(in_10), .in_3(in_11), .in_4(in_12), .in_5(in_13), .in_6({8{1'b0}}), .in_7({8{1'b0}}),
    .in_8({8{1'b0}}), .Select(Select[2:0]), .out_10(mult_8x1x8_2_out_10));
  Mult_2x1x8 mult_2x1x8_1 (.out_4(out_15), ._0(mult_8x1x8_1_out_10), ._1(mult_8x1x8_2_out_10), .in_3(Select[3]));

  // Notes on the sheet:
  //   0
  //   1
  //   2
  //   3
  //   4
  //   5
  //   6
  //   7
  //   8
  //   9
  //   10
  //   11
  //   12
  //   Saida
endmodule
