// Logisim project detector numero primo.circ as structural Verilog: 1 circuit, main circuit detector de numero primo
module detector_de_numero_primo (
  input  A,
  input  B,
  input  C,
  input  D,
  output out_5
);

  wire and_1_out, and_2_out, and_3_out, and_4_out;

  and and_1 (and_1_out, ~A, ~B, C);  // AND_Gate
  and and_2 (and_2_out, B, ~C, D);  // AND_Gate
  and and_3 (and_3_out, ~B, C, D);  // AND_Gate
  and and_4 (and_4_out, ~A, B, D);  // AND_Gate
  or or_1 (out_5, and_1_out, and_2_out, and_3_out, and_4_out);
endmodule
