// Logisim project somador8bits+4.circ as structural Verilog: 2 circuits, main circuit main
module main (
  input  [7:0] in_1,
  output [7:0] out_2,
  output out_3
);

  wire somador_1_carry_out, somador_3_carry_out, somador_4_carry_out, somador_5_carry_out,
       somador_6_carry_out, somador_7_carry_out;

  Somador somador_1 (.Carry_in(1'b0), .Entrada(in_1[0]), .\Saída (out_2[0]), .Carry_out(somador_1_carry_out));
  Somador somador_2 (.Carry_in(somador_1_carry_out), .Entrada(in_1[1]), .\Saída (out_2[1]));  // open: Carry_out
  Somador somador_3 (.Carry_in(1'b1), .Entrada(in_1[2]), .\Saída (out_2[2]), .Carry_out(somador_3_carry_out));
  Somador somador_4 (
    .Carry_in(somador_3_carry_out), .Entrada(in_1[3]), .\Saída (out_2[3]), .Carry_out(somador_4_carry_out));
  Somador somador_5 (
    .Carry_in(somador_4_carry_out), .Entrada(in_1[4]), .\Saída (out_2[4]), .Carry_out(somador_5_carry_out));
  Somador somador_6 (
    .Carry_in(somador_5_carry_out), .Entrada(in_1[5]), .\Saída (out_2[5]), .Carry_out(somador_6_carry_out));
  Somador somador_7 (
    .Carry_in(somador_6_carry_out), .Entrada(in_1[6]), .\Saída (out_2[6]), .Carry_out(somador_7_carry_out));
  Somador somador_8 (.Carry_in(somador_7_carry_out), .Entrada(in_1[7]), .\Saída (out_2[7]), .Carry_out(out_3));
endmodule

module Somador (
  input  Carry_in,
  input  Entrada,
  output \Saída ,
  output Carry_out
);

  xor xor_1 (\Saída , Carry_in, Entrada);
  and and_1 (Carry_out, Carry_in, Entrada);
endmodule
