// Logisim project somador8bits.circ as structural Verilog: 2 circuits, main circuit main
module main (
  input  [7:0] in_1,
  input  [7:0] in_2,
  output [7:0] out_3,
  output out_4
);

  wire somador_1_carry_out, somador_2_carry_out, somador_3_carry_out, somador_4_carry_out,
       somador_5_carry_out, somador_6_carry_out, somador_7_carry_out;

  Somador somador_1 (
    .Carry_in(1'b0), .Entrada(in_2[0]), .Entrada_2(in_1[0]), .\Saída (out_3[0]),
    .Carry_out(somador_1_carry_out));
  Somador somador_2 (
    .Carry_in(somador_1_carry_out), .Entrada(in_2[1]), .Entrada_2(in_1[1]), .\Saída (out_3[1]),
    .Carry_out(somador_2_carry_out));
  Somador somador_3 (
    .Carry_in(somador_2_carry_out), .Entrada(in_2[2]), .Entrada_2(in_1[2]), .\Saída (out_3[2]),
    .Carry_out(somador_3_carry_out));
  Somador somador_4 (
    .Carry_in(somador_3_carry_out), .Entrada(in_2[3]), .Entrada_2(in_1[3]), .\Saída (out_3[3]),
    .Carry_out(somador_4_carry_out));
  Somador somador_5 (
    .Carry_in(somador_4_carry_out), .Entrada(in_2[4]), .Entrada_2(in_1[4]), .\Saída (out_3[4]),
    .Carry_out(somador_5_carry_out));
  Somador somador_6 (
    .Carry_in(somador_5_carry_out), .Entrada(in_2[5]), .Entrada_2(in_1[5]), .\Saída (out_3[5]),
    .Carry_out(somador_6_carry_out));
  Somador somador_7 (
    .Carry_in(somador_6_carry_out), .Entrada(in_2[6]), .Entrada_2(in_1[6]), .\Saída (out_3[6]),
    .Carry_out(somador_7_carry_out));
  Somador somador_8 (
    .Carry_in(somador_7_carry_out), .Entrada(in_2[7]), .Entrada_2(in_1[7]), .\Saída (out_3[7]),
    .Carry_out(out_4));
endmodule

module Somador (
  input  Carry_in,
  input  Entrada,
  input  Entrada_2,
  output \Saída ,
  output Carry_out
);

  wire and_1_out, and_2_out, xor_1_out;

  xor xor_1 (xor_1_out, Entrada, Entrada_2);
  xor xor_2 (\Saída , Carry_in, xor_1_out);
  and and_1 (and_1_out, Carry_in, xor_1_out);
  or or_1 (Carry_out, and_1_out, and_2_out);
  and and_2 (and_2_out, Entrada, Entrada_2);
endmodule
